# Fritzing sketch Sonar_Bluetooth_Sketch (saved by Fritzing 1.0.7)
breadboards: 1

parts:
  A1 = Arduino R4 Minima
  R1 = Servo 360º [package=THT]
  A2 = HC-SR04 Ultrasonic Distance Sensor
  BT1 = Bluetooth HC-06u [package=THT]
  Part1 = LCD1602-I2C
  A3 = BBAA100043
  Part2 = KY-006 Passive Buzzer Module [package="Breakout board"]
  R2 = Resistor [tolerance=±5% power=0.25W resistance=220 package=THT]
  R3 = Resistor [tolerance=±5% power=0.25W resistance=220 package=THT]
  R4 = Resistor [tolerance=±5% power=0.25W resistance=220 package=THT]

nets:
  VCC: A1.Pin_5, R1.+, A2.VCC, BT1.VCC, Part1.VCC
  GND: A1.Pin_7, A1.Pin_28, A1.Pin_45, R1.-, A2.GND, BT1.GND, Part1.GND, A3.pin4, Part2.-
  N1: A1.Pin_9, BT1.RXD
  N2: A1.Pin_10, BT1.TXD
  N3: A1.Pin_13, Part1.SDA
  N4: A1.Pin_14, Part1.SCL
  N5: A1.Pin_33, Part2.S
  N6: A1.Pin_34, R4.Pin_1
  N7: A1.Pin_35, R3.Pin_1
  N8: A1.Pin_36, R2.Pin_1
  N9: A1.Pin_41, A2.ECHO
  N10: A1.Pin_42, A2.TRIG
  N11: A1.Pin_43, R1.S
  N12: A3.pin1, R2.Pin_0
  N13: A3.pin2, R3.Pin_0
  N14: A3.pin3, R4.Pin_0

notes:
  Bluebooth mod is only relevant if backend is on the cards
  1k ohm ->
  Lights and buzzer only relevant if bluetooth isnt actual
  LCD might become irrevelevant after bluetooth sonar
  Need 3D printed L bracket for servo to attach the ultrasonic sensor

custom parts:
  Arduino R4 Minima: Introducing the Arduino UNO R4 Minima! This board boasts the RA4M1 microprocessor from Renesas, delivering increased processing power, expanded memory, and additional peripherals.
  Servo 360º: A continuous rotation servo
  HC-SR04 Ultrasonic Distance Sensor: The HC-SR04 is an ultrasonic distance sensor. It is capable of providing measurement for ranges of 2cm to 400cm. The module operates at 5V.
  Bluetooth HC-06u: Bluetooth HC-06 - face up, pins down 16.5mm x 37.5mm PCB
  LCD1602-I2C: A standard character display, usually with 2x16 characters. Comes in many colors with LCM1602 IIC attached.
  BBAA100043: BBAA100043 traffic light module.
  KY-006 Passive Buzzer Module: Passive Piezoelectric Buzzer Module Keyes KY-006, it can produce a range of sound tones depending on the input frequency.
